# Fritzing sketch components (saved by Fritzing 0.9.3b)
breadboards: 1

parts:
  WeMos_D1_Mini2 = WeMos D1 Mini
  Temp_Sensor = BME280 Breakout
  CO2_Sensor = MH-Z19 CO2 sensor [part_number=MH-Z19]
  Display = OLED 128x64 I2C Monochrome Display
  Warning_led = ws2812b [package="smd 2812b"]
  PM2_5_Sensor = SDS011 - dust sensor [part_number=1]
  PIR = RCWL-0516 Microwave Radar Motion Sensor Module
  Temp_sensor = DS18B20 1-Wire Temperature Sensor [part_number=DS18B20]

nets:
  3V3: WeMos_D1_Mini2.3V3, Temp_Sensor.3.3V, Display.VDD
  5V: WeMos_D1_Mini2.5V, CO2_Sensor.Vin, Warning_led.VDD, PM2_5_Sensor.5V, PIR.VIN, Temp_sensor.VDD
  N1: WeMos_D1_Mini2.D0, PIR.OUT
  N2: WeMos_D1_Mini2.D1, Temp_Sensor.SCK/SCL, Display.SDA
  N3: WeMos_D1_Mini2.D2, Temp_Sensor.SDI/SDA, Display.SCK
  N4: WeMos_D1_Mini2.D3, PM2_5_Sensor.TXD
  N5: WeMos_D1_Mini2.D4, Warning_led.DIN
  N6: WeMos_D1_Mini2.D5, CO2_Sensor.TX
  N7: WeMos_D1_Mini2.D6, PM2_5_Sensor.RXD
  N8: WeMos_D1_Mini2.D7, Temp_sensor.DQ
  N9: WeMos_D1_Mini2.D8, CO2_Sensor.RX
  GND: WeMos_D1_Mini2.G, Temp_Sensor.GND, CO2_Sensor.GND, Display.GND, Warning_led.VSS, PM2_5_Sensor.GND, PIR.GND, Temp_sensor.GND

notes:
  not supported yet, reserved for future
  These two are reserved for future

custom parts:
  SDS011 - dust sensor: The SDS 011 Sensor is a quite recent Air Quality Sensor developed by inovafit, a spin-off from the university of Jinan (in Shandong). With its size, it is probably one of the best sensor in terms of accuracy: While other sensors tend to focus on shrinking the sensor size, the SDS 011 has opted for a size tradeoff allowing it to use a larger fan. And the larger the fan, the better the quality.
  RCWL-0516 Microwave Radar Motion Sensor Module: The RCWL-0516 is a microwave radar motion sensor module. Input voltage is 4V to 28V. The 3V3 pin is a power output.
